// Logisim project cpu.circ as structural Verilog: 12 circuits, main circuit main
module main (
  input  _1___jedem
);

  wire clock_1_out, cpu_1_memen, cpu_1_memw, mapper4_1_enable_2;
  wire [3:0] mapper4_1_addrout;
  wire [15:0] cpu_1_dataaddr, cpu_1_datadata, cpu_1_instaddr, leddriver16x16_1_out_6, leddriver16x16_1_out_7,
       leddriver16x16_1_out_8, leddriver16x16_1_out_9, leddriver16x16_1_out_10, leddriver16x16_1_out_11,
       leddriver16x16_1_out_12, leddriver16x16_1_out_13, leddriver16x16_1_out_14, leddriver16x16_1_out_15,
       leddriver16x16_1_out_16, leddriver16x16_1_out_17, leddriver16x16_1_out_18, leddriver16x16_1_out_19,
       leddriver16x16_1_out_20, leddriver16x16_1_out_21, rom_1_data;

  Clock clock_1 (.out(clock_1_out));
  ROM #(.addrWidth(16), .dataWidth(16)) rom_1 (.addr(cpu_1_instaddr), .data(rom_1_data));  // open: sel
  cpu cpu_1 (
    .Rst(_1___jedem), .Clk(clock_1_out), .InstData(rom_1_data), .InstAddr(cpu_1_instaddr),
    .DataData(cpu_1_datadata), .DataAddr(cpu_1_dataaddr), .MemEn(cpu_1_memen), .MemW(cpu_1_memw));
  DotMatrix #(.matrixcols(16), .matrixrows(16)) dotmatrix_1 (
    .col0(leddriver16x16_1_out_6), .col1(leddriver16x16_1_out_7), .col2(leddriver16x16_1_out_8),
    .col3(leddriver16x16_1_out_9), .col4(leddriver16x16_1_out_10), .col5(leddriver16x16_1_out_11),
    .col6(leddriver16x16_1_out_12), .col7(leddriver16x16_1_out_13), .col8(leddriver16x16_1_out_14),
    .col9(leddriver16x16_1_out_15), .col10(leddriver16x16_1_out_16), .col11(leddriver16x16_1_out_17),
    .col12(leddriver16x16_1_out_18), .col13(leddriver16x16_1_out_19), .col14(leddriver16x16_1_out_20),
    .col15(leddriver16x16_1_out_21));
  leddriver16x16 leddriver16x16_1 (
    .data(cpu_1_datadata), .clk(clock_1_out), .en(mapper4_1_enable_2), .w(cpu_1_memw),
    .addr(mapper4_1_addrout), .out_6(leddriver16x16_1_out_6), .out_7(leddriver16x16_1_out_7),
    .out_8(leddriver16x16_1_out_8), .out_9(leddriver16x16_1_out_9), .out_10(leddriver16x16_1_out_10),
    .out_11(leddriver16x16_1_out_11), .out_12(leddriver16x16_1_out_12), .out_13(leddriver16x16_1_out_13),
    .out_14(leddriver16x16_1_out_14), .out_15(leddriver16x16_1_out_15), .out_16(leddriver16x16_1_out_16),
    .out_17(leddriver16x16_1_out_17), .out_18(leddriver16x16_1_out_18), .out_19(leddriver16x16_1_out_19),
    .out_20(leddriver16x16_1_out_20), .out_21(leddriver16x16_1_out_21));
  mapper4 mapper4_1 (
    .AddrIn(cpu_1_dataaddr), .AddrStart({12{1'b0}}), .enable(cpu_1_memen), .AddrOut(mapper4_1_addrout),
    .enable_2(mapper4_1_enable_2));

  // Notes on the sheet:
  //   contents of rom_1 (hex, n*v repeats v):
  //   5d0 808 ff83 100a 652 100a 652 808 183 100a 652 100a 652 100a 652 100a 652 100a 652 808 ffff 100a
  //   652 100a 652 808 c180 100a 652 100a 652 100a 652 100a 652 100a 652 808 c1ff 100a 652 100a 652 800 2b
endmodule

// ALU
module alu (
  input  [15:0] Source,
  input  [15:0] Destination,
  input  [3:0] Op,
  output [15:0] Out,
  output Zero
);

  wire [15:0] adder_1_out, adder_2_out, nand_1_out, negator_1_out, shifter_1_out, shifter_2_out,
       subtractor_1_out, subtractor_2_out;

  Shifter #(.width(16), .shift("lr")) shifter_1 (.in(Source), .\dist (4'b0001), .out(shifter_1_out));
  Shifter #(.width(16)) shifter_2 (.in(Source), .\dist (4'b0001), .out(shifter_2_out));
  Adder #(.width(16)) adder_1 (.a(Destination), .b(Source), .out(adder_1_out), .cin(1'b0));  // open: cout
  Subtractor #(.width(16)) subtractor_1 (
    .a(Destination), .b(Source), .out(subtractor_1_out), .bin(1'b0));  // open: bout
  Negator #(.width(16)) negator_1 (.in(Source), .out(negator_1_out));
  assign nand_1_out = ~(Destination & Source);  // NAND_Gate nand_1, 16 bits wide
  Adder #(.width(16)) adder_2 (.a(Source), .b(16'h1), .out(adder_2_out));  // open: cin, cout
  Subtractor #(.width(16)) subtractor_2 (.a(Source), .b(16'h1), .out(subtractor_2_out));  // open: bin, bout
  Multiplexer #(.select(4), .width(16), .enable("false")) multiplexer_1 (
    .in0(Source), .in1(shifter_1_out), .in2(shifter_2_out), .in3(adder_1_out), .in4(subtractor_1_out),
    .in5(nand_1_out), .in6(negator_1_out), .in7({16{1'b0}}), .in8(16'h1), .in9(adder_2_out),
    .in10(subtractor_2_out), .out(Out), .sel(Op));  // open: in11, in12, in13, in14, in15
  nor nor_1 (Zero, 1'b0, Out[15], Out[14], Out[13], Out[12], Out[11], Out[10], Out[9], Out[8], Out[7], Out[6], Out[5], Out[4], Out[3], Out[2], Out[1], Out[0]);
endmodule

// Regs
module register_bank (
  input  WEn,
  input  [15:0] DstIn,
  input  IPAutoInc,
  input  Reset,
  input  Clk,
  input  [2:0] DstSel,
  input  [2:0] SrcSel,
  output [15:0] DstOut,
  output [15:0] SrcOut,
  output [15:0] IP,
  output [15:0] SP
);

  wire demultiplexer_1_out0, demultiplexer_1_out1, demultiplexer_1_out2, demultiplexer_1_out3,
       demultiplexer_1_out4, demultiplexer_1_out5, demultiplexer_1_out6, demultiplexer_1_out7, not_1_out,
       not_2_out, or_1_out;
  wire [15:0] adder_16_1_1_out, multiplexer_2_out, register_1_q, register_2_q, register_3_q, register_4_q,
       register_5_q, register_6_q;

  Demultiplexer #(.select(3)) demultiplexer_1 (
    .out0(demultiplexer_1_out0), .out1(demultiplexer_1_out1), .out2(demultiplexer_1_out2),
    .out3(demultiplexer_1_out3), .out4(demultiplexer_1_out4), .out5(demultiplexer_1_out5),
    .out6(demultiplexer_1_out6), .out7(demultiplexer_1_out7), .in(WEn), .sel(DstSel));  // open: en
  Multiplexer #(.select(3), .width(16)) multiplexer_1 (
    .in0(IP), .in1(SP), .in2(register_1_q), .in3(register_2_q), .in4(register_3_q), .in5(register_4_q),
    .in6(register_5_q), .in7(register_6_q), .out(DstOut), .sel(DstSel));  // open: en
  adder_16_1 adder_16_1_1 (.In(IP), .CIn(1'b1), .Out(adder_16_1_1_out));  // open: COut
  or or_1 (or_1_out, IPAutoInc, demultiplexer_1_out0);
  not not_1 (not_1_out, demultiplexer_1_out0);
  Multiplexer #(.width(16)) multiplexer_2 (
    .in0(DstIn), .in1(adder_16_1_1_out), .out(multiplexer_2_out), .sel(not_1_out));  // open: en
  not not_2 (not_2_out, Reset);
  Register #(.width(16)) u_IP (.D(multiplexer_2_out), .en(or_1_out), .Q(IP), .clk(Clk), .clr(not_2_out));
  Multiplexer #(.select(3), .width(16)) multiplexer_3 (
    .in0(IP), .in1(SP), .in2(register_1_q), .in3(register_2_q), .in4(register_3_q), .in5(register_4_q),
    .in6(register_5_q), .in7(register_6_q), .out(SrcOut), .sel(SrcSel));  // open: en
  Register #(.width(16)) u_SP (.D(DstIn), .en(demultiplexer_1_out1), .Q(SP), .clk(Clk), .clr(not_2_out));
  Register #(.width(16)) register_1 (
    .D(DstIn), .en(demultiplexer_1_out2), .Q(register_1_q), .clk(Clk), .clr(not_2_out));
  Register #(.width(16)) register_2 (
    .D(DstIn), .en(demultiplexer_1_out3), .Q(register_2_q), .clk(Clk), .clr(not_2_out));
  Register #(.width(16)) register_3 (
    .D(DstIn), .en(demultiplexer_1_out4), .Q(register_3_q), .clk(Clk), .clr(not_2_out));
  Register #(.width(16)) register_4 (
    .D(DstIn), .en(demultiplexer_1_out5), .Q(register_4_q), .clk(Clk), .clr(not_2_out));
  Register #(.width(16)) register_5 (
    .D(DstIn), .en(demultiplexer_1_out6), .Q(register_5_q), .clk(Clk), .clr(not_2_out));
  Register #(.width(16)) register_6 (
    .D(DstIn), .en(demultiplexer_1_out7), .Q(register_6_q), .clk(Clk), .clr(not_2_out));
  // Probe on IP
  // Probe on SP
  // Probe on register_1_q
  // Probe on register_2_q
  // Probe on register_3_q
  // Probe on register_4_q
  // Probe on register_5_q
  // Probe on register_6_q
endmodule

// Ctrl
module cpu_controller (
  input  Reset,
  input  Clk,
  input  [15:0] IP,
  input  [15:0] Inst,
  output RegsWEn,
  output [2:0] SrcSel,
  output [2:0] DstSel,
  output [3:0] AluOp,
  output [15:0] DbOut,
  output MemClk,
  output [15:0] Addr,
  output MemW,
  output DstToData,
  output AluToData,
  output IPAutoInc
);

  wire not_1_out, not_2_out, not_3_out;
  wire [15:0] Data_q, multiplexer_1_out, register_2_q, rom_1_data, rom_1_data_2;
  wire [15:6] register_1_q;

  not not_1 (not_1_out, Reset);
  not not_2 (not_2_out, rom_1_data[1]);
  Register #(.width(16)) register_1 (
    .D(Inst), .en(not_2_out), .Q({register_1_q, DstSel, SrcSel}), .clk(Clk), .clr(not_1_out));
  Multiplexer #(.width(16)) multiplexer_1 (
    .in0(rom_1_data_2), .in1({{10{1'b1}}, Inst[15:10]}), .out(multiplexer_1_out), .sel(rom_1_data[2]));  // open: en
  Register #(.width(16)) Data (.D(Inst), .en(rom_1_data[1]), .Q(Data_q), .clk(Clk), .clr(not_1_out));
  Register #(.width(16)) register_2 (.D(multiplexer_1_out), .Q(register_2_q), .clk(Clk), .clr(not_3_out));  // open: en
  not not_3 (not_3_out, Reset);
  ROM #(.addrWidth(16), .dataWidth(32)) rom_1 (
    .addr(register_2_q),
    .data({rom_1_data_2, rom_1_data[15:9], MemW, MemClk, RegsWEn, DstToData, AluToData, IPAutoInc, rom_1_data[2:0]}));  // open: sel
  assign DbOut = rom_1_data[9] ? Data_q : 16'bz;  // Controlled_Buffer controlled_buffer_1
  Multiplexer #(.width(4)) multiplexer_2 (
    .in0(register_1_q[9:6]), .in1(4'b0000), .out(AluOp), .sel(rom_1_data[10]));  // open: en

  assign Addr = IP;

  // Notes on the sheet:
  //   contents of rom_1 (hex, n*v repeats v):
  //   10004 248 48 65469*0 8 58 1000a 20080 1a8
endmodule

module cpu (
  input  Rst,
  input  Clk,
  input  [15:0] InstData,
  output [15:0] DataData,
  output [15:0] InstAddr,
  output [15:0] DataAddr,
  output MemEn,
  output MemW
);

  wire cpu_controller_1_alutodata, cpu_controller_1_dsttodata, cpu_controller_1_ipautoinc,
       cpu_controller_1_regswen, not_1_out;
  wire [2:0] cpu_controller_1_dstsel, cpu_controller_1_srcsel;
  wire [3:0] cpu_controller_1_aluop;
  wire [15:0] alu_1_out, register_bank_1_dstout, register_bank_1_ip;

  Pull_Resistor #(.pull(1)) pull_resistor_1 (.node(Rst));
  not not_1 (not_1_out, Clk);
  register_bank register_bank_1 (
    .WEn(cpu_controller_1_regswen), .DstIn(DataData), .Clk(not_1_out), .SrcSel(cpu_controller_1_srcsel),
    .DstOut(register_bank_1_dstout), .SrcOut(DataAddr), .IP(register_bank_1_ip),
    .DstSel(cpu_controller_1_dstsel), .IPAutoInc(cpu_controller_1_ipautoinc), .Reset(Rst));  // open: SP
  cpu_controller cpu_controller_1 (
    .Reset(Rst), .Clk(Clk), .IP(register_bank_1_ip), .Inst(InstData), .Addr(InstAddr),
    .RegsWEn(cpu_controller_1_regswen), .SrcSel(cpu_controller_1_srcsel), .DstSel(cpu_controller_1_dstsel),
    .AluOp(cpu_controller_1_aluop), .DbOut(DataData), .MemClk(MemEn), .MemW(MemW),
    .DstToData(cpu_controller_1_dsttodata), .AluToData(cpu_controller_1_alutodata),
    .IPAutoInc(cpu_controller_1_ipautoinc));
  alu alu_1 (
    .Source(DataAddr), .Out(alu_1_out), .Op(cpu_controller_1_aluop), .Destination(register_bank_1_dstout));  // open: Zero
  assign DataData = cpu_controller_1_dsttodata ? register_bank_1_dstout : 16'bz;  // Controlled_Buffer controlled_buffer_1
  assign DataData = cpu_controller_1_alutodata ? alu_1_out : 16'bz;  // Controlled_Buffer controlled_buffer_2
  Pull_Resistor pull_resistor_2 (.node(MemW));
  Pull_Resistor pull_resistor_3 (.node(DataAddr));
  Pull_Resistor pull_resistor_4 (.node(DataData));
  Pull_Resistor pull_resistor_5 (.node(MemEn));

  // Notes on the sheet:
  //   DataBus
  //   AddressBus
endmodule

module adder_1_1 (
  input  A,
  input  B,
  output S,
  output C
);

  xor xor_1 (S, A, B);
  and and_1 (C, A, B);
endmodule

module adder_4_1 (
  input  [3:0] In,
  input  CIn,
  output Cout,
  output [3:0] Sum
);

  wire adder_1_1_1_c, adder_1_1_2_c, adder_1_1_3_c;

  adder_1_1 adder_1_1_1 (.A(In[0]), .B(CIn), .S(Sum[0]), .C(adder_1_1_1_c));
  adder_1_1 adder_1_1_2 (.A(In[2]), .B(adder_1_1_3_c), .S(Sum[2]), .C(adder_1_1_2_c));
  adder_1_1 adder_1_1_3 (.A(In[1]), .B(adder_1_1_1_c), .S(Sum[1]), .C(adder_1_1_3_c));
  adder_1_1 adder_1_1_4 (.A(In[3]), .B(adder_1_1_2_c), .S(Sum[3]), .C(Cout));
endmodule

module adder_16_1 (
  input  [15:0] In,
  input  CIn,
  output COut,
  output [15:0] Out
);

  wire adder_4_1_1_cout, adder_4_1_2_cout, adder_4_1_3_cout;

  adder_4_1 adder_4_1_1 (.In(In[7:4]), .CIn(adder_4_1_2_cout), .Cout(adder_4_1_1_cout), .Sum(Out[7:4]));
  adder_4_1 adder_4_1_2 (.In(In[3:0]), .CIn(CIn), .Cout(adder_4_1_2_cout), .Sum(Out[3:0]));
  adder_4_1 adder_4_1_3 (.In(In[11:8]), .CIn(adder_4_1_1_cout), .Cout(adder_4_1_3_cout), .Sum(Out[11:8]));
  adder_4_1 adder_4_1_4 (.In(In[15:12]), .CIn(adder_4_1_3_cout), .Cout(COut), .Sum(Out[15:12]));
endmodule

module mapper4 (
  input  [15:0] AddrIn,
  input  [11:0] AddrStart,
  input  enable,
  output [3:0] AddrOut,
  output enable_2
);

  wire comparator_1_eq;

  Comparator #(.width(12), .mode("unsigned")) comparator_1 (
    .a(AddrIn[15:4]), .b(AddrStart), .eq(comparator_1_eq));  // open: gt, lt
  and and_1 (enable_2, comparator_1_eq, enable);

  assign AddrOut = AddrIn[3:0];
endmodule

module mapper8 (
  input  [15:0] AddrIn,
  input  [7:0] AddrStart,
  input  enable,
  output [7:0] AddrOut,
  output enable_2
);

  wire comparator_1_eq;

  Comparator #(.mode("unsigned")) comparator_1 (.a(AddrIn[15:8]), .b(AddrStart), .eq(comparator_1_eq));  // open: gt, lt
  and and_1 (enable_2, comparator_1_eq, enable);

  assign AddrOut = AddrIn[7:0];
endmodule

module mapper12 (
  input  [15:0] AddrIn,
  input  [3:0] AddrStart,
  input  enable,
  output [11:0] AddrOut,
  output enable_2
);

  wire comparator_1_eq;

  Comparator #(.width(4), .mode("unsigned")) comparator_1 (
    .a(AddrIn[15:12]), .b(AddrStart), .eq(comparator_1_eq));  // open: gt, lt
  and and_1 (enable_2, comparator_1_eq, enable);

  assign AddrOut = AddrIn[11:0];
endmodule

module leddriver16x16 (
  input  [15:0] data,
  input  clk,
  input  en,
  input  w,
  input  [3:0] addr,
  output [15:0] out_6,
  output [15:0] out_7,
  output [15:0] out_8,
  output [15:0] out_9,
  output [15:0] out_10,
  output [15:0] out_11,
  output [15:0] out_12,
  output [15:0] out_13,
  output [15:0] out_14,
  output [15:0] out_15,
  output [15:0] out_16,
  output [15:0] out_17,
  output [15:0] out_18,
  output [15:0] out_19,
  output [15:0] out_20,
  output [15:0] out_21
);

  wire and_1_out, demultiplexer_1_out0, demultiplexer_1_out1, demultiplexer_1_out2, demultiplexer_1_out3,
       demultiplexer_1_out4, demultiplexer_1_out5, demultiplexer_1_out6, demultiplexer_1_out7,
       demultiplexer_1_out8, demultiplexer_1_out9, demultiplexer_1_out10, demultiplexer_1_out11,
       demultiplexer_1_out12, demultiplexer_1_out13, demultiplexer_1_out14, demultiplexer_1_out15;

  Demultiplexer #(.select(4)) demultiplexer_1 (
    .out0(demultiplexer_1_out0), .out1(demultiplexer_1_out1), .out2(demultiplexer_1_out2),
    .out3(demultiplexer_1_out3), .out4(demultiplexer_1_out4), .out5(demultiplexer_1_out5),
    .out6(demultiplexer_1_out6), .out7(demultiplexer_1_out7), .out8(demultiplexer_1_out8),
    .out9(demultiplexer_1_out9), .out10(demultiplexer_1_out10), .out11(demultiplexer_1_out11),
    .out12(demultiplexer_1_out12), .out13(demultiplexer_1_out13), .out14(demultiplexer_1_out14),
    .out15(demultiplexer_1_out15), .in(and_1_out), .sel(addr));  // open: en
  and and_1 (and_1_out, en, w);
  Register #(.width(16)) register_1 (.D(data), .en(demultiplexer_1_out0), .Q(out_6), .clk(clk));  // open: clr
  Register #(.width(16)) register_2 (.D(data), .en(demultiplexer_1_out1), .Q(out_7), .clk(clk));  // open: clr
  Register #(.width(16)) register_3 (.D(data), .en(demultiplexer_1_out2), .Q(out_8), .clk(clk));  // open: clr
  Register #(.width(16)) register_4 (.D(data), .en(demultiplexer_1_out3), .Q(out_9), .clk(clk));  // open: clr
  Register #(.width(16)) register_5 (.D(data), .en(demultiplexer_1_out4), .Q(out_10), .clk(clk));  // open: clr
  Register #(.width(16)) register_6 (.D(data), .en(demultiplexer_1_out5), .Q(out_11), .clk(clk));  // open: clr
  Register #(.width(16)) register_7 (.D(data), .en(demultiplexer_1_out6), .Q(out_12), .clk(clk));  // open: clr
  Register #(.width(16)) register_8 (.D(data), .en(demultiplexer_1_out7), .Q(out_13), .clk(clk));  // open: clr
  Register #(.width(16)) register_9 (.D(data), .en(demultiplexer_1_out8), .Q(out_14), .clk(clk));  // open: clr
  Register #(.width(16)) register_10 (.D(data), .en(demultiplexer_1_out9), .Q(out_15), .clk(clk));  // open: clr
  Register #(.width(16)) register_11 (.D(data), .en(demultiplexer_1_out10), .Q(out_16), .clk(clk));  // open: clr
  Register #(.width(16)) register_12 (.D(data), .en(demultiplexer_1_out11), .Q(out_17), .clk(clk));  // open: clr
  Register #(.width(16)) register_13 (.D(data), .en(demultiplexer_1_out12), .Q(out_18), .clk(clk));  // open: clr
  Register #(.width(16)) register_14 (.D(data), .en(demultiplexer_1_out13), .Q(out_19), .clk(clk));  // open: clr
  Register #(.width(16)) register_15 (.D(data), .en(demultiplexer_1_out14), .Q(out_20), .clk(clk));  // open: clr
  Register #(.width(16)) register_16 (.D(data), .en(demultiplexer_1_out15), .Q(out_21), .clk(clk));  // open: clr
endmodule
